// Logisim project pc.circ as structural Verilog: 4 circuits, main circuit main
module main (
);

  wire button_1_out, clock_1_out, sevensegmentdriver_1_a, sevensegmentdriver_1_b, sevensegmentdriver_1_c,
       sevensegmentdriver_1_d, sevensegmentdriver_1_e, sevensegmentdriver_1_f, sevensegmentdriver_1_g,
       sevensegmentdriver_2_a, sevensegmentdriver_2_b, sevensegmentdriver_2_c, sevensegmentdriver_2_d,
       sevensegmentdriver_2_e, sevensegmentdriver_2_f, sevensegmentdriver_2_g, sevensegmentdriver_3_a,
       sevensegmentdriver_3_b, sevensegmentdriver_3_c, sevensegmentdriver_3_d, sevensegmentdriver_3_e,
       sevensegmentdriver_3_f, sevensegmentdriver_3_g;
  wire [3:0] doubledabble_1_hundreds, doubledabble_1_ones, doubledabble_1_tens;

  Button button_1 (.out(button_1_out));
  Clock clock_1 (.out(clock_1_out));
  countr countr_1 (.LOAD(button_1_out), .CLK(clock_1_out));  // open: P, Q
  _7_Segment_Display u_7_segment_display_1 (
    .g(sevensegmentdriver_1_g), .f(sevensegmentdriver_1_f), .a(sevensegmentdriver_1_a),
    .b(sevensegmentdriver_1_b), .e(sevensegmentdriver_1_e), .d(sevensegmentdriver_1_d),
    .c(sevensegmentdriver_1_c));  // open: dp
  _7_Segment_Display u_7_segment_display_2 (
    .g(sevensegmentdriver_2_g), .f(sevensegmentdriver_2_f), .a(sevensegmentdriver_2_a),
    .b(sevensegmentdriver_2_b), .e(sevensegmentdriver_2_e), .d(sevensegmentdriver_2_d),
    .c(sevensegmentdriver_2_c));  // open: dp
  SevenSegmentDriver sevensegmentdriver_1 (
    .in_1(doubledabble_1_ones), .F(sevensegmentdriver_1_f), .G(sevensegmentdriver_1_g),
    .A(sevensegmentdriver_1_a), .B(sevensegmentdriver_1_b), .C(sevensegmentdriver_1_c),
    .D(sevensegmentdriver_1_d), .E(sevensegmentdriver_1_e));
  _7_Segment_Display u_7_segment_display_3 (
    .g(sevensegmentdriver_3_g), .f(sevensegmentdriver_3_f), .a(sevensegmentdriver_3_a),
    .b(sevensegmentdriver_3_b), .e(sevensegmentdriver_3_e), .d(sevensegmentdriver_3_d),
    .c(sevensegmentdriver_3_c));  // open: dp
  SevenSegmentDriver sevensegmentdriver_2 (
    .in_1(doubledabble_1_tens), .F(sevensegmentdriver_2_f), .G(sevensegmentdriver_2_g),
    .A(sevensegmentdriver_2_a), .B(sevensegmentdriver_2_b), .C(sevensegmentdriver_2_c),
    .D(sevensegmentdriver_2_d), .E(sevensegmentdriver_2_e));
  SevenSegmentDriver sevensegmentdriver_3 (
    .in_1(doubledabble_1_hundreds), .F(sevensegmentdriver_3_f), .G(sevensegmentdriver_3_g),
    .A(sevensegmentdriver_3_a), .B(sevensegmentdriver_3_b), .C(sevensegmentdriver_3_c),
    .D(sevensegmentdriver_3_d), .E(sevensegmentdriver_3_e));
  DoubleDabble doubledabble_1 (
    .Ones(doubledabble_1_ones), .Tens(doubledabble_1_tens), .Hundreds(doubledabble_1_hundreds));  // open: in_1
endmodule

module countr (
  input  LOAD,
  input  CLK,
  input  [11:0] P,
  output [11:0] Q
);

  wire CARRY1, CARRY2, n74161_1_pin1, n74161_1_pin7, n74161_1_pin10, n74161_2_pin1, n74161_2_pin10,
       n74161_3_pin1, n74161_3_pin7, n74161_3_pin10, SPE;

  not not_1 (SPE, LOAD);
  _74161 u_74161_1 (
    .pin1(n74161_1_pin1), .pin2(CLK), .pin3(P[0]), .pin4(P[1]), .pin5(P[2]), .pin6(P[3]),
    .pin7(n74161_1_pin7), .pin15(CARRY1), .pin14(Q[0]), .pin13(Q[1]), .pin12(Q[2]), .pin11(Q[3]),
    .pin10(n74161_1_pin10), .pin9(SPE));
  _74161 u_74161_2 (
    .pin1(n74161_2_pin1), .pin2(CLK), .pin3(P[4]), .pin4(P[5]), .pin5(P[6]), .pin6(P[7]), .pin7(CARRY1),
    .pin15(CARRY2), .pin14(Q[4]), .pin13(Q[5]), .pin12(Q[6]), .pin11(Q[7]), .pin10(n74161_2_pin10), .pin9(SPE));
  _74161 u_74161_3 (
    .pin1(n74161_3_pin1), .pin2(CLK), .pin3(P[8]), .pin4(P[9]), .pin5(P[10]), .pin6(P[11]),
    .pin7(n74161_3_pin7), .pin14(Q[8]), .pin13(Q[9]), .pin12(Q[10]), .pin11(Q[11]), .pin10(n74161_3_pin10),
    .pin9(SPE));  // open: pin15
  and and_1 (n74161_3_pin7, CARRY1, CARRY2);
  // also tied to VCC on the sheet: {n74161_1_pin1, n74161_1_pin10, n74161_1_pin7, n74161_2_pin1, n74161_2_pin10, n74161_3_pin1, n74161_3_pin10}

  // Notes on the sheet:
  //   LOAD: pull=up
  //   CLK: pull=up
endmodule

module SevenSegmentDriver (
  input  [3:0] in_1,
  output F,
  output G,
  output A,
  output B,
  output C,
  output D,
  output E
);

  wire n7447_1_pin9, n7447_1_pin10, n7447_1_pin11, n7447_1_pin12, n7447_1_pin13, n7447_1_pin14, n7447_1_pin15;

  not not_1 (F, n7447_1_pin15);
  _7447 u_7447_1 (
    .pin1(in_1[1]), .pin2(in_1[2]), .pin6(in_1[3]), .pin7(in_1[0]), .pin15(n7447_1_pin15),
    .pin14(n7447_1_pin14), .pin13(n7447_1_pin13), .pin12(n7447_1_pin12), .pin11(n7447_1_pin11),
    .pin10(n7447_1_pin10), .pin9(n7447_1_pin9));  // open: pin3, pin4, pin5
  not not_2 (G, n7447_1_pin14);
  not not_3 (A, n7447_1_pin13);
  not not_4 (B, n7447_1_pin12);
  not not_5 (C, n7447_1_pin11);
  not not_6 (D, n7447_1_pin10);
  not not_7 (E, n7447_1_pin9);
endmodule

module DoubleDabble (
  input  [7:0] in_1,
  output [3:0] Ones,
  output [3:0] Tens,
  output [3:0] Hundreds
);

  ROM #(.addrWidth(13)) rom_1 (.addr({{5{1'b0}}, in_1}), .data({Tens, Ones}));
  ROM #(.addrWidth(13), .dataWidth(4), .misaligned("true")) rom_2 (.addr({{5{1'b0}}, in_1}), .data(Hundreds));

  // Notes on the sheet:
  //   in_1: pull=down
  //   Ones: pull=down
  //   Tens: pull=down
  //   Hundreds: pull=down
  //   contents of rom_1 (hex, n*v repeats v):
  //   0 1 2 3 4 5 6 7 8 9 10 11 12 13 14 15 16 17 18 19 20 21 22 23 24 25 26 27 28 29 30 31 32 33 34 35 36
  //   37 38 39 40 41 42 43 44 45 46 47 48 49 50 51 52 53 54 55 56 57 58 59 60 61 62 63 64 65 66 67 68 69
  //   70 71 72 73 74 75 76 77 78 79 80 81 82 83 84 85 86 87 88 89 90 91 92 93 94 95 96 97 98 99 0 1 2 3 4
  //   5 6 7 8 9 10 11 12 13 14 15 16 17 18 19 20 21 22 23 24 25 26 27 28 29 30 31 32 33 34 35 36 37 38 39
  //   40 41 42 43 44 45 46 47 48 49 50 51 52 53 54 55 56 57 58 59 60 61 62 63 64 65 66 67 68 69 70 71 72
  //   73 74 75 76 77 78 79 80 81 82 83 84 85 86 87 88 89 90 91 92 93 94 95 96 97 98 99 0 1 2 3 4 5 6 7 8 9
  //   10 11 12 13 14 15 16 17 18 19 20 21 22 23 24 25 26 27 28 29 30 31 32 33 34 35 36 37 38 39 40 41 42
  //   43 44 45 46 47 48 49 50 51 52 53 54 55
  //   contents of rom_2 (hex, n*v repeats v):
  //   100*0 100*1 56*2
endmodule
